// Logisim project cpu.circ as structural Verilog: 20 circuits, main circuit main
module main (
  input  Jen,
  input  rst,
  input  clk,
  input  [31:0] Jin,
  input  in_5,
  input  in_6,
  input  in_7,
  output InstDone,
  output [31:0] R1,
  output [31:0] R2,
  output [31:0] R3,
  output [31:0] Jout,
  output [31:0] R4,
  output [31:0] R5,
  output [31:0] R6,
  output [31:0] R7,
  output [31:0] R8,
  output [31:0] R9,
  output [31:0] R10,
  output [31:0] R11,
  output [31:0] R12,
  output [31:0] R13,
  output [31:0] R14,
  output [31:0] R15,
  output [31:0] R16,
  output [31:0] R17,
  output [31:0] R18,
  output [31:0] R19,
  output [31:0] R20,
  output [31:0] R21,
  output [31:0] R22,
  output [31:0] R23,
  output [31:0] R24,
  output [31:0] R25,
  output [31:0] R26,
  output [31:0] R27,
  output [31:0] R28,
  output [31:0] R29,
  output [31:0] R30,
  output [31:0] R31
);

  wire aluSrc, aluu_zero, and_1_out, and_2_out, and_3_out, and_4_out, and_5_out, branch, clk_t,
       comparator_1_eq, in_controller_1_clk_out, in_controller_1_sda_out, isShift, jr, jump,
       led_controller_1_clk_out, led_controller_1_sda_out, led_controller_2_clk_out,
       led_controller_2_sda_out, link, memToReg, memWrite, not_1_out, not_3_out, not_4_out, not_5_out,
       not_6_out, nZero, pull_resistor_2_node, regDest, regHalt, regWrite, slt;
  wire [0:0] pull_resistor_1_node;
  wire [1:0] aluOp;
  wire [3:0] alu_control_alu_control;
  wire [4:0] multiplexer_6_out, multiplexer_7_out, rd, rs, rt;
  wire [5:0] funct, opcode;
  wire [6:0] keyboard_1_data;
  wire [7:0] led_controller_1_data_out, led_controller_2_data_out, register_1_q;
  wire [8:0] adder_2_out, multiplexer_1_out, multiplexer_2_out, multiplexer_3_out, pc1, PC_q;
  wire [8:6] jumpAddr;
  wire [9:0] addr;
  wire [10:9] rom_1_data;
  wire [31:0] bit_extender_3_out, DMem_dout, i2c_ctrl_q, imm, jout_t, memD, multiplexer_4_out,
       multiplexer_5_out, multiplexer_8_out, multiplexer_9_out, read1, read2, shamt;
  wire [31:10] aluD;

  Clock clock_1 (.out(clk_t));
  Register #(.width(9)) PC (.D(multiplexer_3_out), .en(InstDone), .clk(clk_t), .Q(PC_q), .clr(in_7));
  Adder #(.width(9)) adder_1 (.a(9'h1), .b(PC_q), .out(pc1));  // open: cin, cout
  ROM #(.addrWidth(9), .dataWidth(32)) rom_1 (.addr(PC_q), .data({opcode, rs, rt, rd, rom_1_data, jumpAddr, funct}));
  Adder #(.width(9)) adder_2 (.a(pc1), .b(imm[8:0]), .out(adder_2_out));  // open: cin, cout
  and and_1 (and_1_out, branch, nZero);
  Multiplexer #(.width(9)) multiplexer_1 (.in0(pc1), .in1(adder_2_out), .out(multiplexer_1_out), .sel(and_1_out));
  Multiplexer #(.width(9)) multiplexer_2 (
    .in0(multiplexer_1_out), .in1({jumpAddr, funct}), .out(multiplexer_2_out), .sel(jump));
  jtag_ram512 Imem (.clk(clk_t), .Jen(Jen), .Jin(Jin), .Addr(PC_q), .Jout(jout_t));  // open: Din, Wen, Dout
  Multiplexer #(.width(9)) multiplexer_3 (.in0(multiplexer_2_out), .in1(R31[8:0]), .out(multiplexer_3_out), .sel(jr));
  assign shamt = {{27{1'b0}}, {rom_1_data, jumpAddr}};  // Bit_Extender bit_extender_1
  assign imm = {{16{rd[4]}}, {rd, rom_1_data, jumpAddr, funct}};  // Bit_Extender bit_extender_2
  Multiplexer #(.width(32)) multiplexer_4 (.in0({aluD, addr}), .in1(memD), .out(multiplexer_4_out), .sel(memToReg));
  Multiplexer #(.width(32)) multiplexer_5 (
    .in0(multiplexer_4_out), .in1({{23{1'b0}}, pc1}), .out(multiplexer_5_out), .sel(link));
  Multiplexer #(.width(5)) multiplexer_6 (.in0(rt), .in1(rd), .out(multiplexer_6_out), .sel(regDest));
  controller control (
    .opcode(opcode), .ALUSrc(aluSrc), .RegDest(regDest), .MemWrite(memWrite), .MemtoReg(memToReg),
    .RegWrite(regWrite), .ALUop(aluOp), .branch(branch), .jump(jump), .slt(slt), .link(link));  // open: MemRead
  Multiplexer #(.width(5)) multiplexer_7 (
    .in0(multiplexer_6_out), .in1({5{1'b1}}), .out(multiplexer_7_out), .sel(link));
  and and_2 (and_2_out, regWrite, not_1_out);
  not not_1 (not_1_out, regHalt);
  ALUcontrol alu_control (
    .funct(funct), .aluop(aluOp), .alu_control(alu_control_alu_control), .isShift(isShift),
    .regHalt(regHalt), .jr(jr));
  regfile register_file (
    .clk(clk_t), .rst(in_7), .Dwrite(multiplexer_5_out), .Awrite(multiplexer_7_out), .Aread0(rs),
    .Aread1(rt), .WE(and_2_out), .Dread0(read1), .Dread1(read2), .R1(R1), .R2(R2), .R3(R3), .R4(R4), .R5(R5),
    .R6(R6), .R7(R7), .R8(R8), .R9(R9), .R10(R10), .R11(R11), .R12(R12), .R13(R13), .R14(R14), .R15(R15),
    .R16(R16), .R17(R17), .R18(R18), .R19(R19), .R20(R20), .R21(R21), .R22(R22), .R23(R23), .R24(R24),
    .R25(R25), .R26(R26), .R27(R27), .R28(R28), .R29(R29), .R30(R30), .R31(R31));
  Multiplexer #(.width(32)) multiplexer_8 (.in0(imm), .in1(read2), .out(multiplexer_8_out), .sel(aluSrc));
  Multiplexer #(.width(32)) multiplexer_9 (.in0(read1), .in1(shamt), .out(multiplexer_9_out), .sel(isShift));
  ALU aluu (
    .a(multiplexer_9_out), .b(multiplexer_8_out), .alu_control(alu_control_alu_control), .slt(slt),
    .clk(clk_t), .rst(in_7), .isShift(isShift), .res_low({aluD, addr}), .zero(aluu_zero), .done(InstDone));  // open: output_inverted, output_inc, res_high
  not not_2 (nZero, aluu_zero);
  and and_3 (and_3_out, not_3_out, memWrite);
  not not_3 (not_3_out, addr[9]);
  and and_4 (and_4_out, addr[9], memWrite);
  Register #(.width(32)) i2c_ctrl (.D(read2), .en(and_4_out), .clk(clk_t), .Q(i2c_ctrl_q), .clr(in_7));
  jtag_ram512 DMem (
    .clk(clk_t), .Jen(Jen), .Din(read2), .Jin(jout_t), .Wen(and_3_out), .Addr(addr[8:0]), .Jout(Jout),
    .Dout(DMem_dout));
  Pull_Resistor #(.pull(1)) pull_resistor_1 (.node(pull_resistor_1_node[0]));
  assign pull_resistor_1_node[0] = not_4_out ? 1'b0 : 1'bz;  // Controlled_Buffer controlled_buffer_1
  not not_4 (not_4_out, in_5);
  Pull_Resistor #(.pull(1)) pull_resistor_2 (.node(pull_resistor_2_node));
  assign pull_resistor_2_node = not_5_out ? 1'b0 : 1'bz;  // Controlled_Buffer controlled_buffer_2
  not not_5 (not_5_out, in_6);
  Multiplexer #(.width(32)) multiplexer_10 (.in0(DMem_dout), .in1(bit_extender_3_out), .out(memD), .sel(addr[9]));
  assign bit_extender_3_out = {{30{1'b0}}, {1'b0, pull_resistor_1_node[0]}};  // Bit_Extender bit_extender_3
  In_controller in_controller_1 (
    .scl(pull_resistor_2_node), .sda(pull_resistor_1_node[0]), .rst(in_7), .addr({8{1'b1}}),
    .data_in({1'b0, keyboard_1_data}), .clk_out(in_controller_1_clk_out), .sda_out(in_controller_1_sda_out));  // open: st, clr_out
  assign pull_resistor_1_node[0] = in_controller_1_sda_out ? 1'b0 : 1'bz;  // Controlled_Buffer controlled_buffer_3
  Keyboard keyboard_1 (.clk(in_controller_1_clk_out), .re(1'b1), .clr(in_7), .data(keyboard_1_data));  // open: avail
  LED_controller led_controller_1 (
    .scl(pull_resistor_2_node), .sda(pull_resistor_1_node[0]), .rst(in_7), .available(1'b1),
    .addr({8{1'b0}}), .clk_out(led_controller_1_clk_out), .sda_out(led_controller_1_sda_out),
    .data_out(led_controller_1_data_out));  // open: clr_out
  assign pull_resistor_1_node[0] = led_controller_1_sda_out ? 1'b0 : 1'bz;  // Controlled_Buffer controlled_buffer_4
  TTY tty_1 (.data(led_controller_1_data_out[6:0]), .clk(led_controller_1_clk_out), .we(1'b1), .clr(in_7));
  LED_controller led_controller_2 (
    .scl(pull_resistor_2_node), .sda(pull_resistor_1_node[0]), .rst(in_7), .available(1'b1), .addr(8'h1),
    .clk_out(led_controller_2_clk_out), .sda_out(led_controller_2_sda_out),
    .data_out(led_controller_2_data_out));  // open: clr_out
  assign pull_resistor_1_node[0] = led_controller_2_sda_out ? 1'b0 : 1'bz;  // Controlled_Buffer controlled_buffer_5
  Comparator comparator_1 (.a(led_controller_2_data_out), .b({8{1'b0}}), .eq(comparator_1_eq));  // open: gt, lt
  not not_6 (not_6_out, comparator_1_eq);
  and and_5 (and_5_out, not_6_out, led_controller_2_clk_out);
  Register register_1 (.D(led_controller_2_data_out), .en(1'b1), .clk(and_5_out), .Q(register_1_q), .clr(in_7));
  LED led_1 (.in(register_1_q[0]));
  LED led_2 (.in(register_1_q[1]));
  LED led_3 (.in(register_1_q[2]));
  LED led_4 (.in(register_1_q[3]));

  // Other names for the same wires on the sheet: jumpAddr[5:0] = funct; aluD[9:0] = addr; aluDone = InstDone;
  //   ra[8:0] = R31[8:0]; rst_t = in_7

  // Notes on the sheet:
  //   contents of rom_1 (hex, n*v repeats v):
  //   20080001 ac080200 20080003 ac080200 20100000 200400ff 22050000 c0000d5 1440fffc 8e080000 15000001
  //   8000005 22100004 2009000a 1509fff6 ae000000 20040000 20050000 c000014 8000004 20080002 ac080200
  //   20080000 ac080200 44820 200e0007 20080080 1094024 1c84006 ac080200 21080002 ac080200 2108fffe
  //   ac080200 94840 200e0007 20080080 1094024 1c84006 ac080200 21080002 ac080200 2108fffe ac080200 94840
  //   200e0007 20080080 1094024 1c84006 ac080200 21080002 ac080200 2108fffe ac080200 94840 200e0007
  //   20080080 1094024 1c84006 ac080200 21080002 ac080200 2108fffe ac080200 94840 200e0007 20080080
  //   1094024 1c84006 ac080200 21080002 ac080200 2108fffe ac080200 94840 200e0007 20080080 1094024 1c84006
  //   ac080200 21080002 ac080200 2108fffe ac080200 94840 200e0007 20080080 1094024 1c84006 ac080200
  //   21080002 ac080200 2108fffe ac080200 94840 200e0007 20080080 1094024 1c84006 ac080200 21080002
  //   ac080200 2108fffe ac080200 20080003 ac080200 8c0b0200 20080001 ac080200 15600065 8caa0000 a4820
  //   200e0007 20080080 1094024 1c84006 ac080200 21080002 ac080200 2108fffe ac080200 94840 200e0007
  //   20080080 1094024 1c84006 ac080200 21080002 ac080200 2108fffe ac080200 94840 200e0007 20080080
  //   1094024 1c84006 ac080200 21080002 ac080200 2108fffe ac080200 94840 200e0007 20080080 1094024 1c84006
  //   ac080200 21080002 ac080200 2108fffe ac080200 94840 200e0007 20080080 1094024 1c84006 ac080200
  //   21080002 ac080200 2108fffe ac080200 94840 200e0007 20080080 1094024 1c84006 ac080200 21080002
  //   ac080200 2108fffe ac080200 94840 200e0007 20080080 1094024 1c84006 ac080200 21080002 ac080200
  //   2108fffe ac080200 94840 200e0007 20080080 1094024 1c84006 ac080200 21080002 ac080200 2108fffe
  //   ac080200 20080003 ac080200 8c0b0200 20080001 ac080200 20a50001 1560000d 1540ffa7 20080000 ac080200
  //   20080002 ac080200 20080003 ac080200 8c090200 15200002 20090001 1520fff6 1020 3e00008 20020001
  //   3e00008 20080002 ac080200 20080000 ac080200 44820 200e0007 20080080 1094024 1c84006 ac080200
  //   21080002 ac080200 2108fffe ac080200 94840 200e0007 20080080 1094024 1c84006 ac080200 21080002
  //   ac080200 2108fffe ac080200 94840 200e0007 20080080 1094024 1c84006 ac080200 21080002 ac080200
  //   2108fffe ac080200 94840 200e0007 20080080 1094024 1c84006 ac080200 21080002 ac080200 2108fffe
  //   ac080200 94840 200e0007 20080080 1094024 1c84006 ac080200 21080002 ac080200 2108fffe ac080200 94840
  //   200e0007 20080080 1094024 1c84006 ac080200 21080002 ac080200 2108fffe ac080200 94840 200e0007
  //   20080080 1094024 1c84006 ac080200 21080002 ac080200 2108fffe ac080200 94840 200e0007 20080080
  //   1094024 1c84006 ac080200 21080002 ac080200 2108fffe ac080200 20080003 ac080200 8c0b0200 20080001
  //   ac080200 1560004f 4820 20080003 ac080200 8c0b0200 20080001 ac080200 1604820 94840 20080003 ac080200
  //   8c0b0200 20080001 ac080200 1694820 94840 20080003 ac080200 8c0b0200 20080001 ac080200 1694820 94840
  //   20080003 ac080200 8c0b0200 20080001 ac080200 1694820 94840 20080003 ac080200 8c0b0200 20080001
  //   ac080200 1694820 94840 20080003 ac080200 8c0b0200 20080001 ac080200 1694820 94840 20080003 ac080200
  //   8c0b0200 20080001 ac080200 1694820 94840 20080003 ac080200 8c0b0200 20080001 ac080200 1694820 5820
  //   200e0007 20080080 10b4024 1c84006 ac080200 21080002 ac080200 2108fffe ac080200 aca90000 20080000
  //   ac080200 20080002 ac080200 20080003 ac080200 8c090200 15200002 20090001 1520fff6 1020 3e00008
  //   20020001 3e00008
endmodule

module jtag_ram8 (
  input  clk,
  input  Jen,
  input  [31:0] Din,
  input  [31:0] Jin,
  input  Wen,
  input  [2:0] Addr,
  output [31:0] Dout,
  output [31:0] Jout
);

  wire decoder_1_out0, decoder_1_out1, decoder_1_out2, decoder_1_out3, decoder_1_out4, decoder_1_out5,
       decoder_1_out6, decoder_1_out7, or_1_out, or_2_out, or_3_out, or_4_out, or_5_out, or_6_out, or_7_out,
       or_8_out;
  wire [31:0] M0, M1, M2, M3, M4, M5, M6, multiplexer_1_out, multiplexer_2_out, multiplexer_3_out,
       multiplexer_4_out, multiplexer_5_out, multiplexer_6_out, multiplexer_7_out, multiplexer_8_out;

  Decoder #(.select(3)) decoder_1 (
    .out0(decoder_1_out0), .out1(decoder_1_out1), .out2(decoder_1_out2), .out3(decoder_1_out3),
    .out4(decoder_1_out4), .out5(decoder_1_out5), .out6(decoder_1_out6), .out7(decoder_1_out7), .sel(Addr),
    .en(Wen));
  Multiplexer #(.width(32)) multiplexer_1 (.in0(Din), .in1(Jin), .out(multiplexer_1_out), .sel(Jen));
  Multiplexer #(.width(32)) multiplexer_2 (.in0(Din), .in1(M0), .out(multiplexer_2_out), .sel(Jen));
  Multiplexer #(.width(32)) multiplexer_3 (.in0(Din), .in1(M1), .out(multiplexer_3_out), .sel(Jen));
  Multiplexer #(.width(32)) multiplexer_4 (.in0(Din), .in1(M2), .out(multiplexer_4_out), .sel(Jen));
  Multiplexer #(.width(32)) multiplexer_5 (.in0(Din), .in1(M3), .out(multiplexer_5_out), .sel(Jen));
  Multiplexer #(.width(32)) multiplexer_6 (.in0(Din), .in1(M4), .out(multiplexer_6_out), .sel(Jen));
  Multiplexer #(.width(32)) multiplexer_7 (.in0(Din), .in1(M5), .out(multiplexer_7_out), .sel(Jen));
  Multiplexer #(.width(32)) multiplexer_8 (.in0(Din), .in1(M6), .out(multiplexer_8_out), .sel(Jen));
  Register #(.width(32)) register_1 (.D(multiplexer_1_out), .en(or_1_out), .clk(clk), .Q(M0));  // open: clr
  or or_1 (or_1_out, Jen, decoder_1_out0);
  Register #(.width(32)) register_2 (.D(multiplexer_2_out), .en(or_2_out), .clk(clk), .Q(M1));  // open: clr
  or or_2 (or_2_out, Jen, decoder_1_out1);
  Register #(.width(32)) register_3 (.D(multiplexer_3_out), .en(or_3_out), .clk(clk), .Q(M2));  // open: clr
  or or_3 (or_3_out, Jen, decoder_1_out2);
  Register #(.width(32)) register_4 (.D(multiplexer_4_out), .en(or_4_out), .clk(clk), .Q(M3));  // open: clr
  or or_4 (or_4_out, Jen, decoder_1_out3);
  Register #(.width(32)) register_5 (.D(multiplexer_5_out), .en(or_5_out), .clk(clk), .Q(M4));  // open: clr
  or or_5 (or_5_out, Jen, decoder_1_out4);
  Register #(.width(32)) register_6 (.D(multiplexer_6_out), .en(or_6_out), .clk(clk), .Q(M5));  // open: clr
  or or_6 (or_6_out, Jen, decoder_1_out5);
  Register #(.width(32)) register_7 (.D(multiplexer_7_out), .en(or_7_out), .clk(clk), .Q(M6));  // open: clr
  or or_7 (or_7_out, Jen, decoder_1_out6);
  Register #(.width(32)) register_8 (.D(multiplexer_8_out), .en(or_8_out), .clk(clk), .Q(Jout));  // open: clr
  or or_8 (or_8_out, Jen, decoder_1_out7);
  Multiplexer #(.select(3), .width(32)) multiplexer_9 (
    .in0(M0), .in1(M1), .in2(M2), .in3(M3), .in4(M4), .in5(M5), .in6(M6), .in7(Jout), .out(Dout), .sel(Addr));

  // Other names for the same wires on the sheet: M7[31:0] = Jout
endmodule

module jtag_ram64 (
  input  clk,
  input  Jen,
  input  [31:0] Din,
  input  [31:0] Jin,
  input  Wen,
  input  [5:0] Addr,
  output [31:0] Dout,
  output [31:0] Jout
);

  wire decoder_1_out0, decoder_1_out1, decoder_1_out2, decoder_1_out3, decoder_1_out4, decoder_1_out5,
       decoder_1_out6, decoder_1_out7;
  wire [31:0] b0_dout, b0_jout, b1_dout, b1_jout, b2_dout, b2_jout, b3_dout, b3_jout, b4_dout, b4_jout,
       b5_dout, b5_jout, b6_dout, b6_jout, b7_dout;

  Decoder #(.select(3)) decoder_1 (
    .out0(decoder_1_out0), .out1(decoder_1_out1), .out2(decoder_1_out2), .out3(decoder_1_out3),
    .out4(decoder_1_out4), .out5(decoder_1_out5), .out6(decoder_1_out6), .out7(decoder_1_out7),
    .sel(Addr[5:3]), .en(Wen));
  jtag_ram8 b0 (
    .clk(clk), .Jen(Jen), .Din(Din), .Jin(Jin), .Wen(decoder_1_out0), .Addr(Addr[2:0]), .Dout(b0_dout),
    .Jout(b0_jout));
  jtag_ram8 b1 (
    .clk(clk), .Jen(Jen), .Din(Din), .Jin(b0_jout), .Wen(decoder_1_out1), .Addr(Addr[2:0]), .Dout(b1_dout),
    .Jout(b1_jout));
  jtag_ram8 b2 (
    .clk(clk), .Jen(Jen), .Din(Din), .Jin(b1_jout), .Wen(decoder_1_out2), .Addr(Addr[2:0]), .Dout(b2_dout),
    .Jout(b2_jout));
  jtag_ram8 b3 (
    .clk(clk), .Jen(Jen), .Din(Din), .Jin(b2_jout), .Wen(decoder_1_out3), .Addr(Addr[2:0]), .Dout(b3_dout),
    .Jout(b3_jout));
  jtag_ram8 b4 (
    .clk(clk), .Jen(Jen), .Din(Din), .Jin(b3_jout), .Wen(decoder_1_out4), .Addr(Addr[2:0]), .Dout(b4_dout),
    .Jout(b4_jout));
  jtag_ram8 b5 (
    .clk(clk), .Jen(Jen), .Din(Din), .Jin(b4_jout), .Wen(decoder_1_out5), .Addr(Addr[2:0]), .Dout(b5_dout),
    .Jout(b5_jout));
  jtag_ram8 b6 (
    .clk(clk), .Jen(Jen), .Din(Din), .Jin(b5_jout), .Wen(decoder_1_out6), .Addr(Addr[2:0]), .Dout(b6_dout),
    .Jout(b6_jout));
  jtag_ram8 b7 (
    .clk(clk), .Jen(Jen), .Din(Din), .Jin(b6_jout), .Wen(decoder_1_out7), .Addr(Addr[2:0]), .Dout(b7_dout),
    .Jout(Jout));
  Multiplexer #(.select(3), .width(32)) multiplexer_1 (
    .in0(b0_dout), .in1(b1_dout), .in2(b2_dout), .in3(b3_dout), .in4(b4_dout), .in5(b5_dout), .in6(b6_dout),
    .in7(b7_dout), .out(Dout), .sel(Addr[5:3]));
endmodule

module jtag_ram512 (
  input  clk,
  input  Jen,
  input  [31:0] Din,
  input  [31:0] Jin,
  input  Wen,
  input  [8:0] Addr,
  output [31:0] Jout,
  output [31:0] Dout
);

  wire decoder_1_out0, decoder_1_out1, decoder_1_out2, decoder_1_out3, decoder_1_out4, decoder_1_out5,
       decoder_1_out6, decoder_1_out7;
  wire [31:0] b0_dout, b0_jout, b1_dout, b1_jout, b2_dout, b2_jout, b3_dout, b3_jout, b4_dout, b4_jout,
       b5_dout, b5_jout, b6_dout, b6_jout, b7_dout;

  Decoder #(.select(3)) decoder_1 (
    .out0(decoder_1_out0), .out1(decoder_1_out1), .out2(decoder_1_out2), .out3(decoder_1_out3),
    .out4(decoder_1_out4), .out5(decoder_1_out5), .out6(decoder_1_out6), .out7(decoder_1_out7),
    .sel(Addr[8:6]), .en(Wen));
  jtag_ram64 b0 (
    .clk(clk), .Jen(Jen), .Din(Din), .Jin(Jin), .Wen(decoder_1_out0), .Addr(Addr[5:0]), .Dout(b0_dout),
    .Jout(b0_jout));
  jtag_ram64 b1 (
    .clk(clk), .Jen(Jen), .Din(Din), .Jin(b0_jout), .Wen(decoder_1_out1), .Addr(Addr[5:0]), .Dout(b1_dout),
    .Jout(b1_jout));
  jtag_ram64 b2 (
    .clk(clk), .Jen(Jen), .Din(Din), .Jin(b1_jout), .Wen(decoder_1_out2), .Addr(Addr[5:0]), .Dout(b2_dout),
    .Jout(b2_jout));
  jtag_ram64 b3 (
    .clk(clk), .Jen(Jen), .Din(Din), .Jin(b2_jout), .Wen(decoder_1_out3), .Addr(Addr[5:0]), .Dout(b3_dout),
    .Jout(b3_jout));
  jtag_ram64 b4 (
    .clk(clk), .Jen(Jen), .Din(Din), .Jin(b3_jout), .Wen(decoder_1_out4), .Addr(Addr[5:0]), .Dout(b4_dout),
    .Jout(b4_jout));
  jtag_ram64 b5 (
    .clk(clk), .Jen(Jen), .Din(Din), .Jin(b4_jout), .Wen(decoder_1_out5), .Addr(Addr[5:0]), .Dout(b5_dout),
    .Jout(b5_jout));
  jtag_ram64 b6 (
    .clk(clk), .Jen(Jen), .Din(Din), .Jin(b5_jout), .Wen(decoder_1_out6), .Addr(Addr[5:0]), .Dout(b6_dout),
    .Jout(b6_jout));
  jtag_ram64 b7 (
    .clk(clk), .Jen(Jen), .Din(Din), .Jin(b6_jout), .Wen(decoder_1_out7), .Addr(Addr[5:0]), .Dout(b7_dout),
    .Jout(Jout));
  Multiplexer #(.select(3), .width(32)) multiplexer_1 (
    .in0(b0_dout), .in1(b1_dout), .in2(b2_dout), .in3(b3_dout), .in4(b4_dout), .in5(b5_dout), .in6(b6_dout),
    .in7(b7_dout), .out(Dout), .sel(Addr[8:6]));
endmodule

module controller (
  input  [5:0] opcode,
  output ALUSrc,
  output RegDest,
  output MemRead,
  output MemWrite,
  output MemtoReg,
  output RegWrite,
  output [1:0] ALUop,
  output branch,
  output jump,
  output slt,
  output link
);

  wire comparator_2_eq, comparator_4_eq, undriven, undriven_2;

  ROM #(.addrWidth(6), .dataWidth(1)) AluSrc_dec (.addr(opcode));  // open: data
  ROM #(.addrWidth(6), .dataWidth(1)) regWrite_dec (.addr(opcode));  // open: data
  ROM #(.addrWidth(6), .dataWidth(1)) subAluOp (.addr(opcode));  // open: data
  Comparator #(.width(6)) comparator_1 (.a(opcode), .b(6'b101011), .eq(MemWrite));  // open: gt, lt
  Comparator #(.width(6)) comparator_2 (.a(opcode), .b(6'b100011), .eq(comparator_2_eq));  // open: gt, lt
  or or_1 (MemtoReg, MemWrite, comparator_2_eq);
  not not_1 (RegWrite, undriven);
  Comparator #(.width(6)) comparator_3 (.a(opcode), .b(6'b000101), .eq(branch));  // open: gt, lt
  Comparator #(.width(6)) comparator_4 (.a(opcode), .b(6'b000010), .eq(comparator_4_eq));  // open: gt, lt
  not not_2 (ALUop[1], undriven_2);
  Comparator #(.width(6)) comparator_5 (.a(opcode), .b(6'b001010), .eq(slt));  // open: gt, lt
  Comparator #(.width(6)) comparator_6 (.a(opcode), .b(6'b000011), .eq(link));  // open: gt, lt
  or or_2 (jump, comparator_4_eq, link);

  assign ALUSrc = ALUop[1];
  assign MemRead = 1'b1;
  assign RegDest = ALUop[1];

  // Notes on the sheet:
  //   contents of AluSrc_dec (hex, n*v repeats v):
  //   8*0 1 0 1 24*0 1 7*0 1
  //   contents of regWrite_dec (hex, n*v repeats v):
  //   0 0 1 0 0 1 0 1 35*0 1
  //   contents of subAluOp (hex, n*v repeats v):
  //   5*0 1 4*0 1
endmodule

module regfile (
  input  clk,
  input  rst,
  input  [31:0] Dwrite,
  input  [4:0] Awrite,
  input  [4:0] Aread0,
  input  [4:0] Aread1,
  input  WE,
  output [31:0] Dread0,
  output [31:0] Dread1,
  output [31:0] R1,
  output [31:0] R2,
  output [31:0] R3,
  output [31:0] R4,
  output [31:0] R5,
  output [31:0] R6,
  output [31:0] R7,
  output [31:0] R8,
  output [31:0] R9,
  output [31:0] R10,
  output [31:0] R11,
  output [31:0] R12,
  output [31:0] R13,
  output [31:0] R14,
  output [31:0] R15,
  output [31:0] R16,
  output [31:0] R17,
  output [31:0] R18,
  output [31:0] R19,
  output [31:0] R20,
  output [31:0] R21,
  output [31:0] R22,
  output [31:0] R23,
  output [31:0] R24,
  output [31:0] R25,
  output [31:0] R26,
  output [31:0] R27,
  output [31:0] R28,
  output [31:0] R29,
  output [31:0] R30,
  output [31:0] R31
);

  wire and_1_out, and_2_out, and_3_out, and_4_out, and_5_out, and_6_out, and_7_out, and_8_out, and_9_out,
       and_10_out, and_11_out, and_12_out, and_13_out, and_14_out, and_15_out, and_16_out, and_17_out,
       and_18_out, and_19_out, and_20_out, and_21_out, and_22_out, and_23_out, and_24_out, and_25_out,
       and_26_out, and_27_out, and_28_out, and_29_out, and_30_out, and_31_out, and_32_out, decoder_1_out0,
       decoder_1_out1, decoder_1_out2, decoder_1_out3, decoder_1_out4, decoder_1_out5, decoder_1_out6,
       decoder_1_out7, decoder_2_out0, decoder_2_out1, decoder_2_out2, decoder_2_out3, or_1_out, or_2_out,
       or_3_out, or_4_out, or_5_out, or_6_out, or_7_out, or_8_out, or_9_out, or_10_out, or_11_out, or_12_out,
       or_13_out, or_14_out, or_15_out, or_16_out, or_17_out, or_18_out, or_19_out, or_20_out, or_21_out,
       or_22_out, or_23_out, or_24_out, or_25_out, or_26_out, or_27_out, or_28_out, or_29_out, or_30_out,
       or_31_out, or_32_out, undriven_2, undriven_3, undriven_4, undriven_5;
  wire [31:0] multiplexer_1_out, multiplexer_2_out, multiplexer_3_out, multiplexer_4_out, multiplexer_5_out,
       multiplexer_6_out, multiplexer_7_out, multiplexer_8_out, multiplexer_9_out, undriven;

  Register #(.width(32)) register_1 (.D(undriven), .en(or_1_out), .clk(undriven_2));  // open: Q, clr
  or or_1 (or_1_out, undriven_5, and_1_out);
  and and_1 (and_1_out, undriven_4, undriven_3);
  Decoder #(.select(3)) decoder_1 (
    .out0(decoder_1_out0), .out1(decoder_1_out1), .out2(decoder_1_out2), .out3(decoder_1_out3),
    .out4(decoder_1_out4), .out5(decoder_1_out5), .out6(decoder_1_out6), .out7(decoder_1_out7),
    .sel(Awrite[4:2]), .en(WE));
  Decoder #(.select(2)) decoder_2 (
    .out0(decoder_2_out0), .out1(decoder_2_out1), .out2(decoder_2_out2), .out3(decoder_2_out3),
    .sel(Awrite[1:0]));  // open: en
  Multiplexer #(.width(32)) multiplexer_1 (.in0(Dwrite), .in1({32{1'b0}}), .out(multiplexer_1_out), .sel(rst));
  and and_2 (and_2_out, decoder_2_out0, decoder_1_out1);
  and and_3 (and_3_out, decoder_2_out0, decoder_1_out2);
  and and_4 (and_4_out, decoder_2_out0, decoder_1_out3);
  and and_5 (and_5_out, decoder_2_out0, decoder_1_out4);
  and and_6 (and_6_out, decoder_2_out0, decoder_1_out5);
  and and_7 (and_7_out, decoder_2_out0, decoder_1_out6);
  and and_8 (and_8_out, decoder_2_out0, decoder_1_out7);
  Register #(.width(32)) register_2 (.D(multiplexer_1_out), .en(or_2_out), .clk(clk), .Q(R4));  // open: clr
  or or_2 (or_2_out, rst, and_2_out);
  Register #(.width(32)) register_3 (.D(multiplexer_1_out), .en(or_3_out), .clk(clk), .Q(R8));  // open: clr
  or or_3 (or_3_out, rst, and_3_out);
  Register #(.width(32)) register_4 (.D(multiplexer_1_out), .en(or_4_out), .clk(clk), .Q(R12));  // open: clr
  or or_4 (or_4_out, rst, and_4_out);
  Register #(.width(32)) register_5 (.D(multiplexer_1_out), .en(or_5_out), .clk(clk), .Q(R16));  // open: clr
  or or_5 (or_5_out, rst, and_5_out);
  Register #(.width(32)) register_6 (.D(multiplexer_1_out), .en(or_6_out), .clk(clk), .Q(R20));  // open: clr
  or or_6 (or_6_out, rst, and_6_out);
  Register #(.width(32)) register_7 (.D(multiplexer_1_out), .en(or_7_out), .clk(clk), .Q(R24));  // open: clr
  or or_7 (or_7_out, rst, and_7_out);
  Register #(.width(32)) register_8 (.D(multiplexer_1_out), .en(or_8_out), .clk(clk), .Q(R28));  // open: clr
  or or_8 (or_8_out, rst, and_8_out);
  Multiplexer #(.select(3), .width(32)) multiplexer_2 (
    .in0({32{1'b0}}), .in1(R4), .in2(R8), .in3(R12), .in4(R16), .in5(R20), .in6(R24), .in7(R28),
    .out(multiplexer_2_out), .sel(Aread0[4:2]));
  Multiplexer #(.select(3), .width(32)) multiplexer_3 (
    .in0({32{1'b0}}), .in1(R4), .in2(R8), .in3(R12), .in4(R16), .in5(R20), .in6(R24), .in7(R28),
    .out(multiplexer_3_out), .sel(Aread1[4:2]));
  and and_9 (and_9_out, decoder_2_out1, decoder_1_out0);
  and and_10 (and_10_out, decoder_2_out1, decoder_1_out1);
  and and_11 (and_11_out, decoder_2_out1, decoder_1_out2);
  and and_12 (and_12_out, decoder_2_out1, decoder_1_out3);
  and and_13 (and_13_out, decoder_2_out1, decoder_1_out4);
  and and_14 (and_14_out, decoder_2_out1, decoder_1_out5);
  and and_15 (and_15_out, decoder_2_out1, decoder_1_out6);
  and and_16 (and_16_out, decoder_2_out1, decoder_1_out7);
  Register #(.width(32)) register_9 (.D(multiplexer_1_out), .en(or_9_out), .clk(clk), .Q(R1));  // open: clr
  or or_9 (or_9_out, rst, and_9_out);
  Register #(.width(32)) register_10 (.D(multiplexer_1_out), .en(or_10_out), .clk(clk), .Q(R5));  // open: clr
  or or_10 (or_10_out, rst, and_10_out);
  Register #(.width(32)) register_11 (.D(multiplexer_1_out), .en(or_11_out), .clk(clk), .Q(R9));  // open: clr
  or or_11 (or_11_out, rst, and_11_out);
  Register #(.width(32)) register_12 (.D(multiplexer_1_out), .en(or_12_out), .clk(clk), .Q(R13));  // open: clr
  or or_12 (or_12_out, rst, and_12_out);
  Register #(.width(32)) register_13 (.D(multiplexer_1_out), .en(or_13_out), .clk(clk), .Q(R17));  // open: clr
  or or_13 (or_13_out, rst, and_13_out);
  Register #(.width(32)) register_14 (.D(multiplexer_1_out), .en(or_14_out), .clk(clk), .Q(R21));  // open: clr
  or or_14 (or_14_out, rst, and_14_out);
  Register #(.width(32)) register_15 (.D(multiplexer_1_out), .en(or_15_out), .clk(clk), .Q(R25));  // open: clr
  or or_15 (or_15_out, rst, and_15_out);
  Register #(.width(32)) register_16 (.D(multiplexer_1_out), .en(or_16_out), .clk(clk), .Q(R29));  // open: clr
  or or_16 (or_16_out, rst, and_16_out);
  Multiplexer #(.select(3), .width(32)) multiplexer_4 (
    .in0(R1), .in1(R5), .in2(R9), .in3(R13), .in4(R17), .in5(R21), .in6(R25), .in7(R29),
    .out(multiplexer_4_out), .sel(Aread0[4:2]));
  Multiplexer #(.select(3), .width(32)) multiplexer_5 (
    .in0(R1), .in1(R5), .in2(R9), .in3(R13), .in4(R17), .in5(R21), .in6(R25), .in7(R29),
    .out(multiplexer_5_out), .sel(Aread1[4:2]));
  Register #(.width(32)) register_17 (.D(multiplexer_1_out), .en(or_17_out), .clk(clk), .Q(R2));  // open: clr
  or or_17 (or_17_out, rst, and_17_out);
  and and_17 (and_17_out, decoder_2_out2, decoder_1_out0);
  Register #(.width(32)) register_18 (.D(multiplexer_1_out), .en(or_18_out), .clk(clk), .Q(R6));  // open: clr
  or or_18 (or_18_out, rst, and_18_out);
  and and_18 (and_18_out, decoder_2_out2, decoder_1_out1);
  Register #(.width(32)) register_19 (.D(multiplexer_1_out), .en(or_19_out), .clk(clk), .Q(R10));  // open: clr
  or or_19 (or_19_out, rst, and_19_out);
  and and_19 (and_19_out, decoder_2_out2, decoder_1_out2);
  Register #(.width(32)) register_20 (.D(multiplexer_1_out), .en(or_20_out), .clk(clk), .Q(R14));  // open: clr
  or or_20 (or_20_out, rst, and_20_out);
  and and_20 (and_20_out, decoder_2_out2, decoder_1_out3);
  Register #(.width(32)) register_21 (.D(multiplexer_1_out), .en(or_21_out), .clk(clk), .Q(R18));  // open: clr
  or or_21 (or_21_out, rst, and_21_out);
  and and_21 (and_21_out, decoder_2_out2, decoder_1_out4);
  Register #(.width(32)) register_22 (.D(multiplexer_1_out), .en(or_22_out), .clk(clk), .Q(R22));  // open: clr
  or or_22 (or_22_out, rst, and_22_out);
  and and_22 (and_22_out, decoder_2_out2, decoder_1_out5);
  Register #(.width(32)) register_23 (.D(multiplexer_1_out), .en(or_23_out), .clk(clk), .Q(R26));  // open: clr
  or or_23 (or_23_out, rst, and_23_out);
  and and_23 (and_23_out, decoder_2_out2, decoder_1_out6);
  Register #(.width(32)) register_24 (.D(multiplexer_1_out), .en(or_24_out), .clk(clk), .Q(R30));  // open: clr
  or or_24 (or_24_out, rst, and_24_out);
  and and_24 (and_24_out, decoder_2_out2, decoder_1_out7);
  Multiplexer #(.select(3), .width(32)) multiplexer_6 (
    .in0(R2), .in1(R6), .in2(R10), .in3(R14), .in4(R18), .in5(R22), .in6(R26), .in7(R30),
    .out(multiplexer_6_out), .sel(Aread0[4:2]));
  Multiplexer #(.select(3), .width(32)) multiplexer_7 (
    .in0(R2), .in1(R6), .in2(R10), .in3(R14), .in4(R18), .in5(R22), .in6(R26), .in7(R30),
    .out(multiplexer_7_out), .sel(Aread1[4:2]));
  Register #(.width(32)) register_25 (.D(multiplexer_1_out), .en(or_25_out), .clk(clk), .Q(R3));  // open: clr
  or or_25 (or_25_out, rst, and_25_out);
  and and_25 (and_25_out, decoder_2_out3, decoder_1_out0);
  Register #(.width(32)) register_26 (.D(multiplexer_1_out), .en(or_26_out), .clk(clk), .Q(R7));  // open: clr
  or or_26 (or_26_out, rst, and_26_out);
  and and_26 (and_26_out, decoder_2_out3, decoder_1_out1);
  Register #(.width(32)) register_27 (.D(multiplexer_1_out), .en(or_27_out), .clk(clk), .Q(R11));  // open: clr
  or or_27 (or_27_out, rst, and_27_out);
  and and_27 (and_27_out, decoder_2_out3, decoder_1_out2);
  Register #(.width(32)) register_28 (.D(multiplexer_1_out), .en(or_28_out), .clk(clk), .Q(R15));  // open: clr
  or or_28 (or_28_out, rst, and_28_out);
  and and_28 (and_28_out, decoder_2_out3, decoder_1_out3);
  Register #(.width(32)) register_29 (.D(multiplexer_1_out), .en(or_29_out), .clk(clk), .Q(R19));  // open: clr
  or or_29 (or_29_out, rst, and_29_out);
  and and_29 (and_29_out, decoder_2_out3, decoder_1_out4);
  Register #(.width(32)) register_30 (.D(multiplexer_1_out), .en(or_30_out), .clk(clk), .Q(R23));  // open: clr
  or or_30 (or_30_out, rst, and_30_out);
  and and_30 (and_30_out, decoder_2_out3, decoder_1_out5);
  Register #(.width(32)) register_31 (.D(multiplexer_1_out), .en(or_31_out), .clk(clk), .Q(R27));  // open: clr
  or or_31 (or_31_out, rst, and_31_out);
  and and_31 (and_31_out, decoder_2_out3, decoder_1_out6);
  Register #(.width(32)) register_32 (.D(multiplexer_1_out), .en(or_32_out), .clk(clk), .Q(R31));  // open: clr
  or or_32 (or_32_out, rst, and_32_out);
  and and_32 (and_32_out, decoder_2_out3, decoder_1_out7);
  Multiplexer #(.select(3), .width(32)) multiplexer_8 (
    .in0(R3), .in1(R7), .in2(R11), .in3(R15), .in4(R19), .in5(R23), .in6(R27), .in7(R31),
    .out(multiplexer_8_out), .sel(Aread0[4:2]));
  Multiplexer #(.select(3), .width(32)) multiplexer_9 (
    .in0(R3), .in1(R7), .in2(R11), .in3(R15), .in4(R19), .in5(R23), .in6(R27), .in7(R31),
    .out(multiplexer_9_out), .sel(Aread1[4:2]));
  Multiplexer #(.select(2), .width(32)) multiplexer_10 (
    .in0(multiplexer_2_out), .in1(multiplexer_4_out), .in2(multiplexer_6_out), .in3(multiplexer_8_out),
    .out(Dread0), .sel(Aread0[1:0]));
  Multiplexer #(.select(2), .width(32)) multiplexer_11 (
    .in0(multiplexer_3_out), .in1(multiplexer_5_out), .in2(multiplexer_7_out), .in3(multiplexer_9_out),
    .out(Dread1), .sel(Aread1[1:0]));

  // Notes on the sheet:
  //   Field Template
endmodule

module ALUcontrol (
  input  [5:0] funct,
  input  [1:0] aluop,
  output [3:0] alu_control,
  output isShift,
  output regHalt,
  output jr
);

  wire comparator_1_eq, comparator_2_eq, comparator_3_eq, comparator_4_eq;
  wire [3:0] funct_dec_data;

  Comparator #(.width(6)) comparator_1 (.a(funct), .b(6'b011010), .eq(comparator_1_eq));  // open: gt, lt
  ROM #(.addrWidth(6), .dataWidth(4)) funct_dec (.addr(funct), .data(funct_dec_data));
  Comparator #(.width(6)) comparator_2 (.a(funct), .b(6'b001000), .eq(comparator_2_eq));  // open: gt, lt
  Comparator #(.width(6)) comparator_3 (.a(funct), .b({6{1'b0}}), .eq(comparator_3_eq));  // open: gt, lt
  Comparator #(.width(2)) comparator_4 (.a(aluop), .b(2'b10), .eq(comparator_4_eq));  // open: gt, lt
  and and_1 (jr, comparator_4_eq, comparator_2_eq);
  and and_2 (isShift, comparator_3_eq, comparator_4_eq);
  Multiplexer #(.select(2), .width(4)) multiplexer_1 (
    .in0(4'b0000), .in1(4'b0001), .in2(funct_dec_data), .in3(4'b0001), .out(alu_control), .sel(aluop));
  or or_1 (regHalt, comparator_1_eq, comparator_2_eq);

  // Notes on the sheet:
  //   contents of funct_dec (hex, n*v repeats v):
  //   9 0 0 0 9 0 a b 8*0 e 0 f 7*0 3 7*0 1 0 4 5 6
endmodule

module ALU (
  input  [31:0] a,
  input  [31:0] b,
  input  [3:0] alu_control,
  input  slt,
  input  output_inverted,
  input  output_inc,
  input  clk,
  input  rst,
  input  isShift,
  output [31:0] res_low,
  output zero,
  output [31:0] res_high,
  output done
);

  wire and_2_out, and_3_out, and_4_out, c3_done, comparator_1_eq, comparator_2_eq, comparator_3_lt,
       comparator_4_eq, comparator_5_eq, comparator_6_eq, comparator_7_eq, comparator_8_eq, comparator_8_lt,
       comparator_9_eq, comparator_9_lt, comparator_10_eq, new_input, not_2_out, not_3_out, not_4_out,
       not_6_out, S_op, undriven;
  wire [3:0] register_3_q;
  wire [4:0] c7_cnt, c8_cnt;
  wire [31:0] HILO_q, HILO_q_2, register_1_q, register_2_q;
  wire [63:0] adder_1_out, and_1_out, bit_extender_1_out, bit_extender_2_out, bit_extender_3_out,
       bit_extender_4_out, bit_extender_5_out, bit_extender_8_out, c0_res, c1_res, c2_res, c3_quotient,
       c9_res, c10_res, c11_res, c12_res, hi, lo, multiplexer_1_out, multiplexer_2_out, multiplexer_3_out,
       not_1_out, not_5_out, or_1_out, xor_1_out;

  assign bit_extender_1_out = {{32{1'b0}}, b};  // Bit_Extender bit_extender_1
  assign not_1_out = ~bit_extender_1_out;  // NOT_Gate not_1, 64 bits wide
  assign bit_extender_2_out = {{32{1'b0}}, a};  // Bit_Extender bit_extender_2
  assign bit_extender_3_out = {{32{1'b0}}, b};  // Bit_Extender bit_extender_3
  Register #(.width(32)) register_1 (.D(a), .clk(clk), .Q(register_1_q), .clr(rst));  // open: en
  Register #(.width(32)) register_2 (.D(b), .clk(clk), .Q(register_2_q), .clr(rst));  // open: en
  Carry_Select_Adder c0 (.a(bit_extender_2_out), .b(bit_extender_3_out), .res(c0_res));  // open: c_in
  Carry_Select_Adder c1 (.c_in(1'b1), .a(bit_extender_2_out), .b(not_1_out), .res(c1_res));
  assign and_1_out = bit_extender_2_out & bit_extender_3_out;  // AND_Gate and_1, 64 bits wide
  assign or_1_out = bit_extender_2_out | bit_extender_3_out;  // OR_Gate or_1, 64 bits wide
  assign xor_1_out = bit_extender_2_out ^ bit_extender_3_out;  // XOR_Gate xor_1, 64 bits wide
  Comparator #(.mode("unsigned"), .width(32)) comparator_1 (
    .a(register_1_q), .b(a), .eq(comparator_1_eq));  // open: gt, lt
  Comparator #(.mode("unsigned"), .width(32)) comparator_2 (
    .a(register_2_q), .b(b), .eq(comparator_2_eq));  // open: gt, lt
  Register #(.width(4)) register_3 (.D(alu_control), .en(1'b1), .clk(clk), .Q(register_3_q));  // open: clr
  not not_2 (not_2_out, comparator_1_eq);
  not not_3 (not_3_out, comparator_2_eq);
  S_L_L c9 (.A(a), .shamt(b), .isShift(isShift), .res(c9_res));
  S_R_L c10 (.A(b), .shamt(a[4:0]), .res(c10_res));
  S_R_A c11 (.A(a), .shamt(a[4:0]), .res(c11_res));
  ROTR2 c12 (.A(a), .shamt(a[4:0]), .res(c12_res));
  Comparator #(.width(32)) comparator_3 (.a(a), .b(b), .lt(comparator_3_lt));  // open: gt, eq
  or or_2 (new_input, not_2_out, not_3_out);
  Comparator #(.mode("unsigned"), .width(4)) comparator_4 (
    .a(alu_control), .b(4'b0011), .eq(comparator_4_eq));  // open: gt, lt
  not not_4 (not_4_out, comparator_5_eq);
  Comparator #(.mode("unsigned"), .width(4)) comparator_5 (
    .a(register_3_q), .b(4'b0011), .eq(comparator_5_eq));  // open: gt, lt
  and and_2 (and_2_out, new_input, S_op);
  and and_3 (and_3_out, comparator_4_eq, not_4_out);
  divisor c3 (
    .divisor(b), .dividend(a), .start(and_3_out), .clk(clk), .quotient(c3_quotient[31:0]),
    .remainder(c3_quotient[63:32]), .done(c3_done));
  M_U_L c2 (.a(a), .b(b), .start(undriven), .clk(clk), .res(c2_res));  // open: done
  C_L_O c7 (.in1(a), .S(1'b1), .clk(clk), .En(1'b1), .rst(undriven), .cnt(c7_cnt));  // open: D
  C_L_Z c8 (.in1(a), .S(1'b1), .clk(clk), .En(1'b1), .rst(undriven), .cnt(c8_cnt));  // open: D
  Register #(.width(64)) HILO (.D(c3_quotient), .en(c3_done), .clk(clk), .Q({HILO_q_2, HILO_q}), .clr(rst));
  assign bit_extender_4_out = {{59{c7_cnt[4]}}, c7_cnt};  // Bit_Extender bit_extender_4
  assign bit_extender_5_out = {{59{c8_cnt[4]}}, c8_cnt};  // Bit_Extender bit_extender_5
  assign hi = {{32{HILO_q_2[31]}}, HILO_q_2};  // Bit_Extender bit_extender_6
  assign lo = {{32{HILO_q[31]}}, HILO_q};  // Bit_Extender bit_extender_7
  assign bit_extender_8_out = {{63{1'b0}}, comparator_3_lt};  // Bit_Extender bit_extender_8
  Multiplexer #(.select(4), .width(64)) multiplexer_1 (
    .in0(c0_res), .in1(c1_res), .in2(c2_res), .in4(and_1_out), .in5(or_1_out), .in6(xor_1_out),
    .in7(bit_extender_4_out), .in8(bit_extender_5_out), .in9(c9_res), .in10(c10_res), .in11(c11_res),
    .in12(c12_res), .in13(bit_extender_8_out), .in14(hi), .in15(lo), .out(multiplexer_1_out),
    .sel(alu_control));  // open: in3
  assign not_5_out = ~multiplexer_1_out;  // NOT_Gate not_5, 64 bits wide
  Multiplexer #(.width(64)) multiplexer_2 (
    .in0(multiplexer_1_out), .in1(not_5_out), .out(multiplexer_2_out), .sel(output_inverted));
  Adder #(.width(64)) adder_1 (
    .a(multiplexer_2_out), .b({64{1'b0}}), .out(adder_1_out), .cin(output_inc));  // open: cout
  Multiplexer #(.width(64)) multiplexer_3 (
    .in0(adder_1_out), .in1(bit_extender_8_out), .out(multiplexer_3_out), .sel(slt));
  Comparator #(.width(4)) comparator_6 (.a(alu_control), .b(4'b0011), .eq(comparator_6_eq));  // open: gt, lt
  and and_4 (and_4_out, c3_done, comparator_8_eq);
  not not_6 (not_6_out, comparator_6_eq);
  or or_3 (done, and_4_out, not_6_out);
  Comparator #(.mode("unsigned"), .width(4)) comparator_7 (
    .a(4'b0010), .b(alu_control), .eq(comparator_7_eq));  // open: gt, lt
  Comparator #(.mode("unsigned"), .width(4)) comparator_8 (
    .a(alu_control), .b(4'b0011), .eq(comparator_8_eq), .lt(comparator_8_lt));  // open: gt
  Comparator #(.mode("unsigned"), .width(4)) comparator_9 (
    .a(alu_control), .b(4'b0111), .eq(comparator_9_eq), .lt(comparator_9_lt));  // open: gt
  Comparator #(.mode("unsigned"), .width(4)) comparator_10 (
    .a(alu_control), .b(4'b1000), .eq(comparator_10_eq));  // open: gt, lt
  Multiplexer #(.width(32)) multiplexer_4 (.in0(multiplexer_3_out[31:0]), .out(res_low), .sel(rst));  // open: in1
  Multiplexer #(.width(32)) multiplexer_5 (.in0(multiplexer_3_out[63:32]), .out(res_high), .sel(rst));  // open: in1
  or or_4 (S_op, comparator_7_eq, comparator_9_eq, comparator_10_eq, comparator_8_eq);
  Comparator #(.width(32)) comparator_11 (.a(res_low), .b({32{1'b0}}), .eq(zero));  // open: gt, lt

  // Other names for the same wires on the sheet: aluop[3:0] = alu_control

  // Notes on the sheet:
  //   alu_control: initial=0x3
  //   a: initial=0x63c530c7
  //   b: initial=0x175c9c2e
endmodule

module divisor (
  input  [31:0] divisor,
  input  [31:0] dividend,
  input  start,
  input  clk,
  output [31:0] quotient,
  output [31:0] remainder,
  output done
);

  wire bitselector_1_out, comparator_1_eq, comparator_2_lt, not_1_out, not_2_out;
  wire [6:0] adder_1_out, counter_q, multiplexer_4_out, multiplexer_8_out;
  wire [31:0] A_q, adder_2_out, B_q, bit_extender_1_out, multiplexer_1_out, multiplexer_2_out,
       multiplexer_3_out, multiplexer_5_out, multiplexer_6_out, multiplexer_7_out, multiplexer_9_out,
       multiplexer_10_out, or_1_out, Q_q, shifter_1_out, shifter_2_out, subtractor_1_out;

  Multiplexer #(.width(32)) multiplexer_1 (
    .in0(multiplexer_9_out), .in1({32{1'b0}}), .out(multiplexer_1_out), .sel(start));
  Multiplexer #(.width(32)) multiplexer_2 (.in0(B_q), .in1(divisor), .out(multiplexer_2_out), .sel(start));
  Multiplexer #(.width(32)) multiplexer_3 (
    .in0(multiplexer_10_out), .in1(dividend), .out(multiplexer_3_out), .sel(start));
  Multiplexer #(.width(7)) multiplexer_4 (
    .in0(multiplexer_8_out), .in1({7{1'b0}}), .out(multiplexer_4_out), .sel(start));
  Adder #(.width(7)) adder_1 (.a(counter_q), .b(7'b0000001), .out(adder_1_out));  // open: cin, cout
  Multiplexer #(.width(32)) multiplexer_5 (.in0(multiplexer_1_out), .in1(A_q), .out(multiplexer_5_out), .sel(done));
  Multiplexer #(.width(32)) multiplexer_6 (.in0(multiplexer_2_out), .in1(B_q), .out(multiplexer_6_out), .sel(done));
  Multiplexer #(.width(32)) multiplexer_7 (.in0(multiplexer_3_out), .in1(Q_q), .out(multiplexer_7_out), .sel(done));
  Register #(.width(32)) A (.D(multiplexer_5_out), .en(1'b1), .clk(clk), .Q(A_q));  // open: clr
  Register #(.width(32)) B (.D(multiplexer_6_out), .en(1'b1), .clk(clk), .Q(B_q));  // open: clr
  Register #(.width(32)) Q (.D(multiplexer_7_out), .en(1'b1), .clk(clk), .Q(Q_q));  // open: clr
  Register #(.width(7)) counter (.D(multiplexer_4_out), .en(1'b1), .clk(clk), .Q(counter_q));  // open: clr
  Shifter #(.width(32)) shifter_1 (.in(A_q), .\dist (5'b00001), .out(shifter_1_out));
  BitSelector #(.width(32)) bitselector_1 (.in(Q_q), .out(bitselector_1_out), .sel({5{1'b1}}));
  Comparator #(.mode("unsigned"), .width(7)) comparator_1 (
    .a(counter_q), .b(7'b0100000), .eq(comparator_1_eq));  // open: gt, lt
  assign bit_extender_1_out = {{31{1'b0}}, bitselector_1_out};  // Bit_Extender bit_extender_1
  Adder #(.width(32)) adder_2 (.a(shifter_1_out), .b(bit_extender_1_out), .out(adder_2_out));  // open: cin, cout
  Shifter #(.width(32)) shifter_2 (.in(Q_q), .\dist (5'b00001), .out(shifter_2_out));
  Multiplexer #(.width(7)) multiplexer_8 (
    .in0(adder_1_out), .in1(counter_q), .out(multiplexer_8_out), .sel(comparator_1_eq));
  Subtractor #(.width(32)) subtractor_1 (.a(adder_2_out), .b(B_q), .out(subtractor_1_out));  // open: bin, bout
  Comparator #(.mode("unsigned"), .width(32)) comparator_2 (
    .a(adder_2_out), .b(B_q), .lt(comparator_2_lt));  // open: gt, eq
  not not_1 (not_1_out, comparator_2_lt);
  assign or_1_out = shifter_2_out | 32'h1;  // OR_Gate or_1, 32 bits wide
  and and_1 (done, comparator_1_eq, not_2_out);
  not not_2 (not_2_out, start);
  Multiplexer #(.width(32)) multiplexer_9 (
    .in0(adder_2_out), .in1(subtractor_1_out), .out(multiplexer_9_out), .sel(not_1_out));
  Multiplexer #(.width(32)) multiplexer_10 (
    .in0(shifter_2_out), .in1(or_1_out), .out(multiplexer_10_out), .sel(not_1_out));
  Multiplexer #(.width(32)) multiplexer_11 (.in1(Q_q), .out(quotient), .sel(done));  // open: in0
  Multiplexer #(.width(32)) multiplexer_12 (.in1(A_q), .out(remainder), .sel(done));  // open: in0

  // Notes on the sheet:
  //   divisor: initial=0xc4018d88
  //   dividend: initial=0x82fbf905
  //   clk: initial=0x1
endmodule

module S_R_A (
  input  [31:0] A,
  input  [4:0] shamt,
  output [63:0] res
);

  wire [1:0] stage_1;
  wire [3:0] stage_2;
  wire [7:0] stage_4;
  wire [15:0] stage_8;
  wire [63:0] extended_64, shift_2, shift_4, shift_8, shift_16;

  assign extended_64 = {{32{A[31]}}, A};  // Bit_Extender bit_extender_1
  Multiplexer #(.width(64)) multiplexer_1 (
    .in0({shift_16[63], shift_16[46:0], stage_8}), .in1({{17{shift_16[63]}}, shift_16[46:0]}), .out(res),
    .sel(shamt[4]));
  Multiplexer #(.width(64)) multiplexer_2 (
    .in0(extended_64), .in1({{2{extended_64[63]}}, extended_64[62:1]}),
    .out({shift_2[63], shift_2[60:0], stage_1}), .sel(shamt[0]));
  Multiplexer #(.width(64)) multiplexer_3 (
    .in0({shift_2[63], shift_2[60:0], stage_1}), .in1({{3{shift_2[63]}}, shift_2[60:0]}),
    .out({shift_4[63], shift_4[58:0], stage_2}), .sel(shamt[1]));
  Multiplexer #(.width(64)) multiplexer_4 (
    .in0({shift_4[63], shift_4[58:0], stage_2}), .in1({{5{shift_4[63]}}, shift_4[58:0]}),
    .out({shift_8[63], shift_8[54:0], stage_4}), .sel(shamt[2]));
  Multiplexer #(.width(64)) multiplexer_5 (
    .in0({shift_8[63], shift_8[54:0], stage_4}), .in1({{9{shift_8[63]}}, shift_8[54:0]}),
    .out({shift_16[63], shift_16[46:0], stage_8}), .sel(shamt[3]));

  // Other names for the same wires on the sheet: b0 = shamt[0]; b1 = shamt[1]; b2 = shamt[2]; b3 = shamt[3];
  //   b4 = shamt[4]; shift_1[63:0] = {{2{extended_64[63]}}, extended_64[62:1]};
  //   stage_1[63:2] = {shift_2[63], shift_2[60:0]}; shift_2[62:61] = {2{shift_2[63]}};
  //   stage_2[63:4] = {shift_4[63], shift_4[58:0]}; shift_4[62:59] = {4{shift_4[63]}};
  //   stage_4[63:8] = {shift_8[63], shift_8[54:0]}; shift_8[62:55] = {8{shift_8[63]}};
  //   stage_8[63:16] = {shift_16[63], shift_16[46:0]}; shift_16[62:47] = {16{shift_16[63]}}; stage_16[63:0] = res
endmodule

module S_R_L (
  input  [31:0] A,
  input  [4:0] shamt,
  output [63:0] res
);

  wire [1:0] stage_1;
  wire [3:0] stage_2;
  wire [7:0] stage_4;
  wire [15:0] stage_8;
  wire [47:0] shift_16;
  wire [55:0] shift_8;
  wire [59:0] shift_4;
  wire [61:0] shift_2;
  wire [63:0] extended_64;

  assign extended_64 = {{32{1'b0}}, A};  // Bit_Extender bit_extender_1
  Multiplexer #(.width(64)) multiplexer_1 (
    .in0({shift_16, stage_8}), .in1({{16{1'b0}}, shift_16}), .out(res), .sel(shamt[4]));
  Multiplexer #(.width(64)) multiplexer_2 (
    .in0(extended_64), .in1({1'b0, extended_64[63:1]}), .out({shift_2, stage_1}), .sel(shamt[0]));
  Multiplexer #(.width(64)) multiplexer_3 (
    .in0({shift_2, stage_1}), .in1({2'b00, shift_2}), .out({shift_4, stage_2}), .sel(shamt[1]));
  Multiplexer #(.width(64)) multiplexer_4 (
    .in0({shift_4, stage_2}), .in1({4'b0000, shift_4}), .out({shift_8, stage_4}), .sel(shamt[2]));
  Multiplexer #(.width(64)) multiplexer_5 (
    .in0({shift_8, stage_4}), .in1({{8{1'b0}}, shift_8}), .out({shift_16, stage_8}), .sel(shamt[3]));

  // Other names for the same wires on the sheet: b0 = shamt[0]; b1 = shamt[1]; b2 = shamt[2]; b3 = shamt[3];
  //   b4 = shamt[4]; shift_1[62:0] = extended_64[63:1]; stage_1[63:2] = shift_2; stage_2[63:4] = shift_4;
  //   stage_4[63:8] = shift_8; stage_8[63:16] = shift_16; stage_16[63:0] = res
endmodule

module S_L_L (
  input  [31:0] A,
  input  [31:0] shamt,
  input  isShift,
  output [63:0] res
);

  wire b0, b1, b2, b3, b4;
  wire [31:0] multiplexer_1_out;
  wire [31:5] multiplexer_2_out;
  wire [63:0] extended_64;
  wire [63:2] shift_2;
  wire [63:4] shift_4;
  wire [63:8] shift_8;
  wire [63:16] shift_16;
  wire [63:48] stage_8;
  wire [63:56] stage_4;
  wire [63:60] stage_2;
  wire [63:62] stage_1;

  Multiplexer #(.width(32)) multiplexer_1 (.in0(A), .in1(shamt), .out(multiplexer_1_out), .sel(isShift));
  Multiplexer #(.width(32)) multiplexer_2 (
    .in0(shamt), .in1(A), .out({multiplexer_2_out, b4, b3, b2, b1, b0}), .sel(isShift));
  assign extended_64 = {{32{1'b0}}, multiplexer_1_out};  // Bit_Extender bit_extender_1
  Multiplexer #(.width(64)) multiplexer_3 (
    .in0({stage_8, shift_16}), .in1({shift_16, {16{1'b0}}}), .out(res), .sel(b4));
  Multiplexer #(.width(64)) multiplexer_4 (
    .in0(extended_64), .in1({extended_64[62:0], 1'b0}), .out({stage_1, shift_2}), .sel(b0));
  Multiplexer #(.width(64)) multiplexer_5 (
    .in0({stage_1, shift_2}), .in1({shift_2, 2'b00}), .out({stage_2, shift_4}), .sel(b1));
  Multiplexer #(.width(64)) multiplexer_6 (
    .in0({stage_2, shift_4}), .in1({shift_4, 4'b0000}), .out({stage_4, shift_8}), .sel(b2));
  Multiplexer #(.width(64)) multiplexer_7 (
    .in0({stage_4, shift_8}), .in1({shift_8, {8{1'b0}}}), .out({stage_8, shift_16}), .sel(b3));

  // Other names for the same wires on the sheet: shift_1[63:1] = extended_64[62:0]; stage_2[59:0] = shift_4;
  //   stage_4[55:0] = shift_8; stage_8[47:0] = shift_16; stage_1[61:0] = shift_2; stage_16[63:0] = res
endmodule

module C_L_O (
  input  [31:0] in1,
  input  S,
  input  clk,
  input  En,
  input  rst,
  output [4:0] cnt,
  output D
);

  wire CBO, CHECK, FINAL, INIT, not_1_out, not_2_out, not_3_out, or_1_out, or_2_out, or_3_out, or_4_out,
       R0_bit0, RN_eq_0, SHIFT, T0, T1, T2, T3, T4, T6;
  wire [4:0] adder_1_out, multiplexer_1_out, R1_q, RN_dec, RN_q;
  wire [31:0] multiplexer_2_out, R0_q;
  wire [63:0] c71_res;

  or or_1 (or_1_out, T0, SHIFT);
  D_Flip_Flop u_INIT (.D(T4), .clk(clk), .Q(INIT), .preset(rst));  // open: Qn, reset
  D_Flip_Flop u_CBO (.D(or_1_out), .clk(clk), .Q(CBO), .reset(rst));  // open: Qn, preset
  D_Flip_Flop u_SHIFT (.D(T6), .clk(clk), .Q(SHIFT), .reset(rst));  // open: Qn, preset
  D_Flip_Flop u_FINAL (.D(T1), .clk(clk), .Q(FINAL), .reset(rst));  // open: Qn, preset
  not not_1 (not_1_out, RN_eq_0);
  not not_2 (not_2_out, R0_bit0);
  not not_3 (not_3_out, S);
  and and_1 (T0, INIT, S);
  and and_2 (T1, CHECK, En, RN_eq_0);
  and and_3 (T2, CBO, R0_bit0);
  and and_4 (T3, CBO, not_2_out);
  and and_5 (T4, INIT, not_3_out);
  and and_6 (T6, CHECK, En, not_1_out);
  D_Flip_Flop u_CHECK (.D(CBO), .clk(clk), .Q(CHECK), .reset(rst));  // open: Qn, preset
  or or_2 (or_2_out, T0, SHIFT);
  Multiplexer #(.width(5)) multiplexer_1 (.in0({5{1'b1}}), .in1(RN_dec), .out(multiplexer_1_out), .sel(SHIFT));
  Register #(.width(5)) RN (.D(multiplexer_1_out), .en(or_2_out), .clk(clk), .Q(RN_q));  // open: clr
  or or_3 (or_3_out, T0, SHIFT);
  Multiplexer #(.width(32)) multiplexer_2 (.in0(in1), .in1(c71_res[31:0]), .out(multiplexer_2_out), .sel(SHIFT));
  Subtractor #(.width(5)) subtractor_1 (.a(RN_q), .b(5'b00001), .out(RN_dec));  // open: bin, bout
  Comparator #(.width(5)) comparator_1 (.a(RN_q), .b({5{1'b0}}), .eq(RN_eq_0));  // open: gt, lt
  Register #(.width(32)) R0 (.D(multiplexer_2_out), .en(or_3_out), .clk(clk), .Q(R0_q));  // open: clr
  or or_4 (or_4_out, T3, T0);
  and and_7 (R0_bit0, 1'b1, R0_q[0]);
  Register #(.width(5)) R1 (.D(adder_1_out), .en(T2), .clk(clk), .Q(R1_q), .clr(or_4_out));
  Register #(.width(5)) R2 (.D(R1_q), .en(T1), .clk(clk), .Q(cnt), .clr(rst));
  Register #(.width(1)) RD (.D(1'b1), .en(T1), .clk(clk), .Q(D), .clr(T0));
  S_R_L c71 (.A(R0_q), .shamt(5'b00001), .res(c71_res));
  Adder #(.width(5)) adder_1 (.a(R1_q), .b(5'b00001), .out(adder_1_out));  // open: cin, cout
endmodule

module C_L_Z (
  input  [31:0] in1,
  input  S,
  input  clk,
  input  En,
  input  rst,
  output [4:0] cnt,
  output D
);

  wire CBO, CHECK, FINAL, INIT, not_1_out, not_2_out, not_3_out, not_4_out, or_1_out, or_2_out, or_3_out,
       or_4_out, R0_bit0, RN_eq_0, SHIFT, T0, T1, T2, T3, T4, T6;
  wire [4:0] adder_1_out, multiplexer_1_out, R1_q, RN_dec, RN_q;
  wire [31:0] multiplexer_2_out, R0_q;
  wire [63:0] c71_res;

  or or_1 (or_1_out, T0, SHIFT);
  D_Flip_Flop u_INIT (.D(T4), .clk(clk), .Q(INIT), .preset(rst));  // open: Qn, reset
  D_Flip_Flop u_CBO (.D(or_1_out), .clk(clk), .Q(CBO), .reset(rst));  // open: Qn, preset
  D_Flip_Flop u_SHIFT (.D(T6), .clk(clk), .Q(SHIFT), .reset(rst));  // open: Qn, preset
  D_Flip_Flop u_FINAL (.D(T1), .clk(clk), .Q(FINAL), .reset(rst));  // open: Qn, preset
  not not_1 (not_1_out, RN_eq_0);
  not not_2 (not_2_out, R0_bit0);
  not not_3 (not_3_out, S);
  and and_1 (T0, INIT, S);
  and and_2 (T1, CHECK, En, RN_eq_0);
  and and_3 (T2, CBO, R0_bit0);
  and and_4 (T3, CBO, not_2_out);
  and and_5 (T4, INIT, not_3_out);
  and and_6 (T6, CHECK, En, not_1_out);
  D_Flip_Flop u_CHECK (.D(CBO), .clk(clk), .Q(CHECK), .reset(rst));  // open: Qn, preset
  or or_2 (or_2_out, T0, SHIFT);
  Multiplexer #(.width(5)) multiplexer_1 (.in0({5{1'b1}}), .in1(RN_dec), .out(multiplexer_1_out), .sel(SHIFT));
  Register #(.width(5)) RN (.D(multiplexer_1_out), .en(or_2_out), .clk(clk), .Q(RN_q));  // open: clr
  or or_3 (or_3_out, T0, SHIFT);
  Multiplexer #(.width(32)) multiplexer_2 (.in0(in1), .in1(c71_res[31:0]), .out(multiplexer_2_out), .sel(SHIFT));
  Subtractor #(.width(5)) subtractor_1 (.a(RN_q), .b(5'b00001), .out(RN_dec));  // open: bin, bout
  Comparator #(.width(5)) comparator_1 (.a(RN_q), .b({5{1'b0}}), .eq(RN_eq_0));  // open: gt, lt
  Register #(.width(32)) R0 (.D(multiplexer_2_out), .en(or_3_out), .clk(clk), .Q(R0_q));  // open: clr
  or or_4 (or_4_out, T3, T0);
  not not_4 (not_4_out, R0_q[0]);
  Register #(.width(5)) R1 (.D(adder_1_out), .en(T2), .clk(clk), .Q(R1_q), .clr(or_4_out));
  Register #(.width(5)) R2 (.D(R1_q), .en(T1), .clk(clk), .Q(cnt), .clr(rst));
  and and_7 (R0_bit0, 1'b1, not_4_out);
  Register #(.width(1)) RD (.D(1'b1), .en(T1), .clk(clk), .Q(D), .clr(T0));
  S_R_L c71 (.A(R0_q), .shamt(5'b00001), .res(c71_res));
  Adder #(.width(5)) adder_1 (.a(R1_q), .b(5'b00001), .out(adder_1_out));  // open: cin, cout
endmodule

module ROTR2 (
  input  [31:0] A,
  input  [4:0] shamt,
  output [63:0] res
);

  wire [1:0] lsb2;
  wire [3:0] lsb4;
  wire [7:0] lsb8;
  wire [15:0] lsb16;
  wire [47:0] shift_16;
  wire [55:0] shift_8;
  wire [59:0] shift_4;
  wire [61:0] shift_2;
  wire [63:0] extended_64, stage_16;

  assign extended_64 = {{32{1'b0}}, A};  // Bit_Extender bit_extender_1
  Multiplexer #(.width(64)) multiplexer_1 (
    .in0({shift_16, lsb16}), .in1({lsb16, shift_16}), .out(stage_16), .sel(shamt[4]));
  Multiplexer #(.width(64)) multiplexer_2 (
    .in0(extended_64), .in1({extended_64[0], extended_64[63:1]}), .out({shift_2, lsb2}), .sel(shamt[0]));
  Multiplexer #(.width(64)) multiplexer_3 (
    .in0({shift_2, lsb2}), .in1({lsb2, shift_2}), .out({shift_4, lsb4}), .sel(shamt[1]));
  Multiplexer #(.width(64)) multiplexer_4 (
    .in0({shift_4, lsb4}), .in1({lsb4, shift_4}), .out({shift_8, lsb8}), .sel(shamt[2]));
  Multiplexer #(.width(64)) multiplexer_5 (
    .in0({shift_8, lsb8}), .in1({lsb8, shift_8}), .out({shift_16, lsb16}), .sel(shamt[3]));
  assign res[31:0] = stage_16[31:0] | stage_16[63:32];  // OR_Gate or_1, 32 bits wide

  assign res[63:32] = {32{1'b0}};

  // Other names for the same wires on the sheet: b0 = shamt[0]; b1 = shamt[1]; b2 = shamt[2]; b3 = shamt[3];
  //   b4 = shamt[4]; shift_1[63:0] = {extended_64[0], extended_64[63:1]}; lsb1 = extended_64[0];
  //   stage_1[63:0] = {shift_2, lsb2}; stage_2[63:0] = {shift_4, lsb4}; shift_4[63:60] = lsb4;
  //   stage_4[63:0] = {shift_8, lsb8}; shift_8[63:56] = lsb8; stage_8[63:0] = {shift_16, lsb16};
  //   shift_2[63:62] = lsb2; shift_16[63:48] = lsb16
endmodule

module Carry_Save_Adder (
  input  c_in,
  input  [63:0] a,
  input  [63:0] b,
  input  [63:0] c,
  output [63:0] res
);

  wire [63:0] and_1_out, and_2_out, and_3_out, carry_out, shifter_1_out, xor_1_out, xor_2_out;

  assign xor_1_out = b ^ c;  // XOR_Gate xor_1, 64 bits wide
  assign and_1_out = a & b;  // AND_Gate and_1, 64 bits wide
  assign and_2_out = a & c;  // AND_Gate and_2, 64 bits wide
  assign and_3_out = b & c;  // AND_Gate and_3, 64 bits wide
  assign xor_2_out = a ^ xor_1_out;  // XOR_Gate xor_2, 64 bits wide
  assign carry_out = and_1_out | and_2_out | and_3_out;  // OR_Gate carry, 64 bits wide
  Shifter #(.width(64)) shifter_1 (.in(carry_out), .\dist (6'b000001), .out(shifter_1_out));
  Carry_Select_Adder c22 (.c_in(c_in), .a(xor_2_out), .b(shifter_1_out), .res(res));
endmodule

module Carry_Select_Adder (
  input  c_in,
  input  [63:0] a,
  input  [63:0] b,
  output [63:0] res
);

  wire adder_1_cout, adder_2_cout, adder_3_cout, adder_4_cout, adder_5_cout, adder_6_cout, adder_8_cout,
       adder_9_cout, adder_10_cout, adder_11_cout, adder_12_cout, adder_13_cout, adder_14_cout,
       multiplexer_1_out, multiplexer_2_out, multiplexer_3_out, multiplexer_4_out, multiplexer_5_out,
       multiplexer_6_out;
  wire [7:0] adder_1_out, adder_2_out, adder_3_out, adder_4_out, adder_5_out, adder_6_out, adder_7_out,
       adder_9_out, adder_10_out, adder_11_out, adder_12_out, adder_13_out, adder_14_out, adder_15_out;

  Adder adder_1 (.a(a[15:8]), .b(b[15:8]), .out(adder_1_out), .cout(adder_1_cout));  // open: cin
  Adder adder_2 (.a(a[23:16]), .b(b[23:16]), .out(adder_2_out), .cout(adder_2_cout));  // open: cin
  Adder adder_3 (.a(a[31:24]), .b(b[31:24]), .out(adder_3_out), .cout(adder_3_cout));  // open: cin
  Adder adder_4 (.a(a[39:32]), .b(b[39:32]), .out(adder_4_out), .cout(adder_4_cout));  // open: cin
  Adder adder_5 (.a(a[47:40]), .b(b[47:40]), .out(adder_5_out), .cout(adder_5_cout));  // open: cin
  Adder adder_6 (.a(a[55:48]), .b(b[55:48]), .out(adder_6_out), .cout(adder_6_cout));  // open: cin
  Adder adder_7 (.a(a[63:56]), .b(b[63:56]), .out(adder_7_out));  // open: cin, cout
  Adder adder_8 (.a(a[7:0]), .b(b[7:0]), .out(res[7:0]), .cin(c_in), .cout(adder_8_cout));
  Adder adder_9 (.a(a[15:8]), .b(b[15:8]), .out(adder_9_out), .cin(1'b1), .cout(adder_9_cout));
  Adder adder_10 (.a(a[23:16]), .b(b[23:16]), .out(adder_10_out), .cin(1'b1), .cout(adder_10_cout));
  Adder adder_11 (.a(a[31:24]), .b(b[31:24]), .out(adder_11_out), .cin(1'b1), .cout(adder_11_cout));
  Adder adder_12 (.a(a[39:32]), .b(b[39:32]), .out(adder_12_out), .cin(1'b1), .cout(adder_12_cout));
  Adder adder_13 (.a(a[47:40]), .b(b[47:40]), .out(adder_13_out), .cin(1'b1), .cout(adder_13_cout));
  Adder adder_14 (.a(a[55:48]), .b(b[55:48]), .out(adder_14_out), .cin(1'b1), .cout(adder_14_cout));
  Adder adder_15 (.a(a[63:56]), .b(b[63:56]), .out(adder_15_out), .cin(1'b1));  // open: cout
  Multiplexer multiplexer_1 (.in0(adder_1_cout), .in1(adder_9_cout), .out(multiplexer_1_out), .sel(adder_8_cout));
  Multiplexer multiplexer_2 (.in0(adder_2_cout), .in1(adder_10_cout), .out(multiplexer_2_out), .sel(multiplexer_1_out));
  Multiplexer multiplexer_3 (.in0(adder_3_cout), .in1(adder_11_cout), .out(multiplexer_3_out), .sel(multiplexer_2_out));
  Multiplexer multiplexer_4 (.in0(adder_4_cout), .in1(adder_12_cout), .out(multiplexer_4_out), .sel(multiplexer_3_out));
  Multiplexer multiplexer_5 (.in0(adder_5_cout), .in1(adder_13_cout), .out(multiplexer_5_out), .sel(multiplexer_4_out));
  Multiplexer multiplexer_6 (.in0(adder_6_cout), .in1(adder_14_cout), .out(multiplexer_6_out), .sel(multiplexer_5_out));
  Multiplexer #(.width(8)) multiplexer_7 (.in0(adder_1_out), .in1(adder_9_out), .out(res[15:8]), .sel(adder_8_cout));
  Multiplexer #(.width(8)) multiplexer_8 (
    .in0(adder_2_out), .in1(adder_10_out), .out(res[23:16]), .sel(multiplexer_1_out));
  Multiplexer #(.width(8)) multiplexer_9 (
    .in0(adder_3_out), .in1(adder_11_out), .out(res[31:24]), .sel(multiplexer_2_out));
  Multiplexer #(.width(8)) multiplexer_10 (
    .in0(adder_4_out), .in1(adder_12_out), .out(res[39:32]), .sel(multiplexer_3_out));
  Multiplexer #(.width(8)) multiplexer_11 (
    .in0(adder_5_out), .in1(adder_13_out), .out(res[47:40]), .sel(multiplexer_4_out));
  Multiplexer #(.width(8)) multiplexer_12 (
    .in0(adder_6_out), .in1(adder_14_out), .out(res[55:48]), .sel(multiplexer_5_out));
  Multiplexer #(.width(8)) multiplexer_13 (
    .in0(adder_7_out), .in1(adder_15_out), .out(res[63:56]), .sel(multiplexer_6_out));
endmodule

module M_U_L (
  input  [31:0] a,
  input  [31:0] b,
  input  start,
  input  clk,
  output [63:0] res,
  output done
);

  wire comparator_1_eq, not_1_out;
  wire [3:0] adder_1_out, counter_q, multiplexer_4_out, multiplexer_8_out;
  wire [4:0] adder_2_out;
  wire [31:0] bit_extender_1_out, bit_extender_2_out, bit_extender_3_out, multiplexer_1_out,
       multiplexer_2_out, multiplexer_5_out, multiplexer_6_out, multiplicand_q, multiplier_q;
  wire [63:0] c25_res, case_01_res, case_10_res, case_11_res, i2, i21, multiplexer_3_out, multiplexer_7_out,
       result, sum;

  Multiplexer #(.width(32)) multiplexer_1 (.in0(multiplicand_q), .in1(a), .out(multiplexer_1_out), .sel(start));
  Multiplexer #(.width(32)) multiplexer_2 (.in0(bit_extender_3_out), .in1(b), .out(multiplexer_2_out), .sel(start));
  Multiplexer #(.width(64)) multiplexer_3 (.in0(result), .in1({64{1'b0}}), .out(multiplexer_3_out), .sel(start));
  Multiplexer #(.width(4)) multiplexer_4 (.in0(adder_1_out), .in1(4'b0000), .out(multiplexer_4_out), .sel(start));
  Multiplexer #(.width(32)) multiplexer_5 (
    .in0(multiplexer_1_out), .in1(multiplicand_q), .out(multiplexer_5_out), .sel(done));
  Multiplexer #(.width(32)) multiplexer_6 (
    .in0(multiplexer_2_out), .in1(multiplier_q), .out(multiplexer_6_out), .sel(done));
  Multiplexer #(.width(64)) multiplexer_7 (.in0(multiplexer_3_out), .in1(sum), .out(multiplexer_7_out), .sel(done));
  Multiplexer #(.width(4)) multiplexer_8 (
    .in0(multiplexer_4_out), .in1(counter_q), .out(multiplexer_8_out), .sel(done));
  Register #(.width(32)) multiplicand (.D(multiplexer_5_out), .clk(clk), .Q(multiplicand_q));  // open: en, clr
  Register #(.width(32)) multiplier (.D(multiplexer_6_out), .clk(clk), .Q(multiplier_q));  // open: en, clr
  Register #(.width(64)) u_sum (.D(multiplexer_7_out), .clk(clk), .Q(sum));  // open: en, clr
  Register #(.width(4)) counter (.D(multiplexer_8_out), .clk(clk), .Q(counter_q));  // open: en, clr
  Comparator #(.mode("unsigned"), .width(4)) comparator_1 (
    .a(counter_q), .b(4'b1111), .eq(comparator_1_eq));  // open: gt, lt
  Adder #(.width(4)) adder_1 (.a(counter_q), .b(4'b0001), .out(adder_1_out));  // open: cin, cout
  assign bit_extender_1_out = {{27{counter_q[3]}}, {counter_q, 1'b0}};  // Bit_Extender bit_extender_1
  assign bit_extender_2_out = {{27{adder_2_out[4]}}, adder_2_out};  // Bit_Extender bit_extender_2
  Adder #(.width(5)) adder_2 (.a({counter_q, 1'b0}), .b(5'b00001), .out(adder_2_out));  // open: cin, cout
  Carry_Select_Adder case_01 (.c_in(1'b0), .a(i2), .b(sum), .res(case_01_res));
  Carry_Select_Adder case_10 (.c_in(1'b0), .a(i21), .b(sum), .res(case_10_res));
  Carry_Save_Adder case_11 (.c_in(1'b0), .a(sum), .b(i2), .c(i21), .res(case_11_res));
  Bit_Extender #(.in_width(64), .out_width(32), .\type ("zero")) bit_extender_3 (
    .in(c25_res), .out(bit_extender_3_out));
  S_R_L c25 (.A(multiplier_q), .shamt(5'b00010), .res(c25_res));
  S_L_L c23 (.A(multiplicand_q), .shamt(bit_extender_1_out), .res(i2));  // open: isShift
  S_L_L c24 (.A(multiplicand_q), .shamt(bit_extender_2_out), .res(i21));  // open: isShift
  Multiplexer #(.select(2), .width(64)) multiplexer_9 (
    .in0(sum), .in1(case_01_res), .in2(case_10_res), .in3(case_11_res), .out(result), .sel(multiplier_q[1:0]));
  not not_1 (not_1_out, start);
  and and_1 (done, comparator_1_eq, not_1_out);
  Multiplexer #(.width(64)) multiplexer_10 (.in0({64{1'b0}}), .in1(result), .out(res), .sel(done));

  // Notes on the sheet:
  //   a: initial=0x39f50473
  //   b: initial=0xdd7199ba
endmodule

module LED_controller (
  input  scl,
  input  sda,
  input  rst,
  input  available,
  input  [7:0] addr,
  output clk_out,
  output sda_out,
  output clr_out,
  output [7:0] data_out
);

  wire addr_c, clr, comparator_1_eq, comparator_2_eq, comparator_3_eq, comparator_4_eq, d_ff_1_q, d_ff_2_q,
       init, not_1_out, terminate;
  wire [1:0] multiplexer_5_out, multiplexer_6_out, or_3_out;
  wire [4:0] adder_1_out, multiplexer_1_out, multiplexer_2_out, multiplexer_3_out, multiplexer_4_out, state_q;

  D_Flip_Flop #(.trigger("falling")) d_ff_1 (.D(scl), .clk(sda), .Q(d_ff_1_q), .preset(rst));  // open: Qn, reset
  D_Flip_Flop d_ff_2 (.D(scl), .clk(sda), .Q(d_ff_2_q), .preset(rst));  // open: Qn, reset
  Register #(.trigger("falling"), .width(5)) state (
    .D(multiplexer_4_out), .en(1'b1), .clk(scl), .Q(state_q), .clr(clr));
  // Shift_Register #(.trigger("falling")) shift_register_1: pin names not known; wires that end beside it: clr, 1'b0, 1'b1, scl, sda, data_out[7]
  Adder #(.width(5)) adder_1 (.a(5'b00001), .b(state_q), .out(adder_1_out));  // open: cin, cout
  not not_1 (not_1_out, sda);
  Multiplexer #(.width(5)) multiplexer_1 (.in0({5{1'b0}}), .in1(5'b01010), .out(multiplexer_1_out), .sel(available));
  and and_1 (init, scl, not_1_out, d_ff_1_q);
  and and_2 (terminate, scl, sda, d_ff_2_q);
  Multiplexer #(.width(5)) multiplexer_2 (.in0({5{1'b0}}), .in1(5'b01010), .out(multiplexer_2_out), .sel(addr_c));
  Comparator #(.width(5)) comparator_1 (.a(state_q), .b(5'b01001), .eq(comparator_1_eq));  // open: gt, lt
  Comparator #(.width(5)) comparator_2 (.a(state_q), .b({5{1'b0}}), .eq(comparator_2_eq));  // open: gt, lt
  Comparator #(.width(5)) comparator_3 (.a(state_q), .b(5'b10010), .eq(comparator_3_eq));  // open: gt, lt
  Comparator comparator_4 (.a({8{1'b1}}), .b(data_out), .eq(comparator_4_eq));  // open: gt, lt
  Comparator comparator_5 (.a(data_out), .b(addr), .eq(addr_c));  // open: gt, lt
  Multiplexer #(.width(5)) multiplexer_3 (.in0({5{1'b0}}), .in1(5'b00001), .out(multiplexer_3_out), .sel(init));
  or or_1 (clr, terminate, rst);
  Multiplexer #(.select(2), .width(5)) multiplexer_4 (
    .in0(adder_1_out), .in1(multiplexer_1_out), .in2(multiplexer_2_out), .in3(multiplexer_3_out),
    .out(multiplexer_4_out), .sel(or_3_out));
  or or_2 (or_3_out[1], comparator_1_eq, comparator_2_eq);
  or or_3 (or_3_out[0], comparator_2_eq, comparator_3_eq);
  and and_3 (clr_out, comparator_3_eq, comparator_4_eq);
  Multiplexer #(.width(2)) multiplexer_5 (.in0(2'b00), .in1(2'b11), .out(multiplexer_5_out), .sel(available));
  Multiplexer #(.width(2)) multiplexer_6 (.in0(2'b00), .in1(2'b10), .out(multiplexer_6_out), .sel(addr_c));
  Multiplexer #(.select(2), .width(2)) multiplexer_7 (
    .in0(2'b00), .in1(multiplexer_5_out), .in2(multiplexer_6_out), .in3(2'b00), .out({sda_out, clk_out}),
    .sel(or_3_out));
endmodule

module In_controller (
  input  scl,
  input  sda,
  input  rst,
  input  [7:0] addr,
  input  [7:0] data_in,
  output clk_out,
  output sda_out,
  output [4:0] st,
  output clr_out
);

  wire ack, addr_c, and_1_out, clr, comparator_1_eq, comparator_3_eq, comparator_4_eq, comparator_5_eq,
       d_ff_1_q, d_ff_2_q, data, init, load, not_1_out, not_3_out, not_4_out, not_5_out, terminate;
  wire [1:0] or_2_out;
  wire [2:0] multiplexer_5_out, multiplexer_6_out;
  wire [4:0] adder_1_out, multiplexer_1_out, multiplexer_2_out, multiplexer_3_out, multiplexer_4_out;
  wire [6:0] dat;
  wire [7:0] not_2_out, undriven;

  not not_1 (not_1_out, load);
  assign not_2_out = ~data_in;  // NOT_Gate not_2, 8 bits wide
  and and_1 (and_1_out, 1'b1, not_1_out);
  Register #(.trigger("falling"), .width(5)) state (.D(multiplexer_4_out), .en(1'b1), .clk(scl), .Q(st), .clr(clr));
  // Shift_Register #(.trigger("falling")) shift_register_1: pin names not known; wires that end beside it: clr, 1'b0, 1'b1, scl, sda
  // Shift_Register #(.trigger("falling")) shift_register_2: pin names not known; wires that end beside it: {clr, dat}, clr, load, and_1_out, scl, 1'b0, data, undriven[7]
  D_Flip_Flop #(.trigger("falling")) d_ff_1 (.D(scl), .clk(sda), .Q(d_ff_1_q), .preset(rst));  // open: Qn, reset
  D_Flip_Flop d_ff_2 (.D(scl), .clk(sda), .Q(d_ff_2_q), .preset(rst));  // open: Qn, reset
  Adder #(.width(5)) adder_1 (.a(5'b00001), .b(st), .out(adder_1_out));  // open: cin, cout
  not not_3 (not_3_out, sda);
  Multiplexer #(.width(5)) multiplexer_1 (.in0({5{1'b0}}), .in1(5'b01010), .out(multiplexer_1_out), .sel(not_3_out));
  not not_4 (not_4_out, sda);
  Multiplexer #(.width(5)) multiplexer_2 (.in0({5{1'b0}}), .in1(5'b01010), .out(multiplexer_2_out), .sel(addr_c));
  Comparator comparator_1 (.a({8{1'b1}}), .b(undriven), .eq(comparator_1_eq));  // open: gt, lt
  Comparator comparator_2 (.a(undriven), .b(addr), .eq(addr_c));  // open: gt, lt
  and and_2 (init, scl, not_4_out, d_ff_1_q);
  and and_3 (terminate, scl, sda, d_ff_2_q);
  Multiplexer #(.width(5)) multiplexer_3 (.in0({5{1'b0}}), .in1(5'b00001), .out(multiplexer_3_out), .sel(init));
  Comparator #(.width(5)) comparator_3 (.a(st), .b(5'b01001), .eq(comparator_3_eq));  // open: gt, lt
  Comparator #(.width(5)) comparator_4 (.a(st), .b({5{1'b0}}), .eq(comparator_4_eq));  // open: gt, lt
  Comparator #(.width(5)) comparator_5 (.a(st), .b(5'b10010), .eq(comparator_5_eq));  // open: gt, lt
  Multiplexer #(.select(2), .width(5)) multiplexer_4 (
    .in0(adder_1_out), .in1(multiplexer_1_out), .in2(multiplexer_2_out), .in3(multiplexer_3_out),
    .out(multiplexer_4_out), .sel(or_2_out));
  or or_1 (or_2_out[1], comparator_3_eq, comparator_4_eq);
  or or_2 (or_2_out[0], comparator_4_eq, comparator_5_eq);
  and and_4 (clr_out, comparator_5_eq, comparator_1_eq);
  or or_3 (clr, terminate, rst);
  not not_5 (not_5_out, sda);
  Multiplexer #(.width(3)) multiplexer_5 (.in0(3'b000), .in1(3'b011), .out(multiplexer_5_out), .sel(not_5_out));
  Comparator #(.width(1)) comparator_6 (.a(undriven[0]), .b(1'b1), .eq(ack));  // open: gt, lt
  Multiplexer #(.width(3)) multiplexer_6 (.in0(3'b000), .in1(3'b110), .out(multiplexer_6_out), .sel(addr_c));
  Multiplexer #(.select(2), .width(3)) multiplexer_7 (
    .in0({data, 2'b00}), .in1(multiplexer_5_out), .in2(multiplexer_6_out), .in3({data, 2'b00}),
    .out({sda_out, load, clk_out}), .sel(or_2_out));
  Keyboard keyboard_1 (.clk(clk_out), .re(1'b1), .data(dat));  // open: clr, avail
endmodule
